// Logisim project BCDsegment.circ as structural Verilog: 2 circuits, main circuit Seg
module Seg (
  input  [3:0] in_1
);

  _7_Segment_Display u_7_segment_display_1 ();  // open: g, f, a, b, e, d, c, dp
endmodule

module BCD (
  input  in_1,
  input  in_2,
  input  in_3,
  input  in_4,
  output a,
  output e,
  output f,
  output g,
  output b,
  output c,
  output d
);

  wire and_1_out, not_1_out, not_2_out, not_3_out, not_4_out;

  not not_1 (not_1_out, in_1);
  not not_2 (not_2_out, in_2);
  not not_3 (not_3_out, in_3);
  not not_4 (not_4_out, in_4);
  and and_1 (and_1_out, in_1, not_2_out, not_3_out, not_4_out);
  // AND_Gate and_2 has open pins: in0=not_1_out, in1=not_2_out, in2=not_3_out, in3=not_4_out, out=open
  // OR_Gate or_1 has open pins: out=a
  // OR_Gate or_2 has open pins: out=b
  // OR_Gate or_3 has open pins: out=c
  // OR_Gate or_4 has open pins: out=d
  // OR_Gate or_5 has open pins: out=e
  // OR_Gate or_6 has open pins: out=f
  // OR_Gate or_7 has open pins: out=g
endmodule
